# Fritzing sketch PCB (saved by Fritzing 0.9.3b)
breadboards: 1

parts:
  FTDI = female pin header, 5 pins [form="♀ (female)"]
  100nF = Ceramic Capacitor [capacitance=100nF package="200 mil [THT, multilayer]"]
  10K = Resistor [tolerance=±5% resistance=10k package=THT]
  ATMEGA328 = atmega328 [package=dip]
  16Mhz = Crystal [frequency="16 Mhz" package=THT]
  22pF = Ceramic Capacitor [capacitance=22µF package="100 mil [THT, multilayer]"]
  22pF_2 = Ceramic Capacitor [capacitance=22µF package="100 mil [THT, multilayer]"]
  10K_2 = Resistor [tolerance=±5% resistance=10k package=THT]
  150_to_162_uH = Inductor [package="400 mil [THT]"]
  2N3904 = NPN-Transistor [package="TO92 [THT]"]
  10nF = Ceramic Capacitor [capacitance=10nF package="200 mil [THT, multilayer]"]
  S1 = Pushbutton [package="[THT]"]
  S2 = Pushbutton [package="[THT]"]
  S3 = Pushbutton [package="[THT]"]
  S4 = Pushbutton [package="[THT]"]
  S5 = Pushbutton [package="[THT]"]
  RFID_READER = female pin header, 5 pins [form="♀ (female)"]
  J2 = female pin header, 2 pins [form="♀ (female)"]  # not connected
  R1 = Resistor [tolerance=±5% resistance=220 package=THT]
  R2 = Resistor [tolerance=±5% resistance=220 package=THT]
  LED1 = LED - 5mm [color="Red (633nm)" package="5 mm [THT]"]
  LED2 = LED - 5mm [color="Red (633nm)" package="5 mm [THT]"]
  S6 = Pushbutton [package="[THT]"]
  OLED = female pin header, 4 pins [form="♀ (female)"]

nets:
  GND: FTDI.pin1, ATMEGA328.GND, 22pF.1, 22pF_2.1, 150_to_162_uH.pin_1, 2N3904.E, 10nF.0, S1.Pin_2, S2.Pin_1, S2.Pin_2, S3.Pin_2, S4.Pin_2, S5.Pin_2, RFID_READER.pin2, LED1.cathode, LED2.cathode, S6.Pin_2, OLED.pin3
  5V: FTDI.pin2, 10K.Pin_0, ATMEGA328.VCC, ATMEGA328.AVCC, ATMEGA328.AREF, RFID_READER.pin1, OLED.pin4
  DTR: FTDI.pin3, 100nF.1
  TX: FTDI.pin4, ATMEGA328.D1_(TX)
  RX: FTDI.pin5, ATMEGA328.D0_(RX)
  N1: 100nF.0, 10K.Pin_1, ATMEGA328.RESET
  TX_RFID: ATMEGA328.D2, RFID_READER.pin5
  BTN_CARD_1: ATMEGA328.D3_(PWM), S1.Pin_3, S1.Pin_4
  BTN_CARD_2: ATMEGA328.D4, S2.Pin_3, S2.Pin_4
  N2: ATMEGA328.XLAT1, 16Mhz.pin_0, 22pF_2.0
  N3: ATMEGA328.XLAT2, 16Mhz.pin_1, 22pF.0
  BTN_CARD_3: ATMEGA328.D5_(PWM), S3.Pin_3, S3.Pin_4
  BTN_CARD_4: ATMEGA328.D6_(PWM), S4.Pin_3, S4.Pin_4
  BTN_CARD_5: ATMEGA328.D7, S6.Pin_3, S6.Pin_4
  BTN_CLONE: ATMEGA328.D8, S5.Pin_3, S5.Pin_4
  ANT: ATMEGA328.D9_(PWM), 10K_2.Pin_0
  PIN_10: ATMEGA328.D10_(PWM), R1.Pin_1
  PIN_11: ATMEGA328.D11_(PWM), R2.Pin_1
  SDA: ATMEGA328.A4, OLED.pin1
  SCL: ATMEGA328.A5, OLED.pin2
  N4: 10K_2.Pin_1, 2N3904.B
  N5: 150_to_162_uH.pin_0, 2N3904.C, 10nF.1
  N6: R1.Pin_0, LED1.anode
  N7: R2.Pin_0, LED2.anode

notes:
  RX TX DTR VCC GND
